# Fritzing sketch Electrical_Scheme (saved by Fritzing 0.9.3b)
breadboards: 1

parts:
  Matrix_keypad1 = KEYPAD 4x4
  PIR1 = PIR sensor
  J1 = Piezo Speaker
  Part1 = Arduino Uno (Rev3)
  R1 = Resistor [tolerance=±5% resistance=1k package="2010 [SMD]"]
  LED1 = LED - 5mm [color="Red (633nm)" package="5 mm [THT]"]
  LED2 = LED - 5mm [color="Green (555nm)" package="5 mm [THT]"]
  R2 = Resistor [tolerance=±5% resistance=1k package="2010 [SMD]"]
  R3 = Resistor [tolerance=±5% resistance=1k package="2010 [SMD]"]
  U1 = LCD-16X2 [package=lcd-16x2_noholes]
  R4 = Resistor [tolerance=±5% resistance=1k package="2010 [SMD]"]
  U2 = POT [package=pot_mammoth]
  U2_2 = POT [package=trim_pot]

nets:
  N1: Matrix_keypad1.col1, Part1.D9_PWM
  N2: Matrix_keypad1.col2, Part1.D8
  N3: Matrix_keypad1.col3, Part1.D7
  N4: Matrix_keypad1.col4, Part1.D6_PWM
  N5: Matrix_keypad1.row1, Part1.D5_PWM
  N6: Matrix_keypad1.row2, Part1.D4
  N7: Matrix_keypad1.row3, Part1.D3_PWM
  N8: Matrix_keypad1.row4, Part1.D2
  5V: PIR1.VDD, Part1.5V, R4.Pin_1
  N9: PIR1.SIG, Part1.D10_PWM/SS
  GND: PIR1.GND, Part1.GND, R1.Pin_1, U1.VSS, U1.R_W, U1.K, U2.A, U2_2.A
  N10: J1.pin1, R1.Pin_0
  N11: J1.pin2, Part1.D11_PWM/MOSI
  N12: Part1.A0, U1.RS
  N13: Part1.A1, U1.E
  N14: Part1.A2, U1.DB4
  N15: Part1.A3, U1.DB5
  N16: Part1.A4/SDA, U1.DB6
  N17: Part1.A5/SCL, U1.DB7
  N18: Part1.D12/MISO, R2.Pin_0
  N19: Part1.D13/SCK, R3.Pin_0
  N20: LED1.cathode, LED2.cathode
  N21: LED1.anode, R2.Pin_1
  N22: LED2.anode, R3.Pin_1
  N23: U1.VDD, U2.E, U2_2.E
  N24: U1.VO, U2.S, U2_2.S
  N25: U1.A, R4.Pin_0

custom parts:
  KEYPAD 4x4: Matrix keypad 16 buttons, 4 rows x 4 columns
